# Fritzing sketch esquema (saved by Fritzing 0.9.1b)
breadboards: 1

parts:
  Parte1 = Arduino Uno (Rev3)
  S1 = Square Pushbutton
  R1 = Resistor [tolerance=±5% resistance=10k package=THT]
  K1 = Keyes Relay [package=THT]

nets:
  N1: Parte1.D13/SCK, K1.signal
  N2: Parte1.D2, S1.leg0, R1.Pin_1
  N3: Parte1.5V, S1.leg1, K1.power
  N4: Parte1.GND, R1.Pin_0, K1.ground

custom parts:
  Keyes Relay: The Keyes 5V relay module is suitable for SCM development, home appliance control. It uses a 5V~12V TIL control signal which can control DC / AC signal.
