# Fritzing sketch esquema2_ (saved by Fritzing 0.9.1b)
breadboards: 1

parts:
  Part2 = Arduino Uno (Rev3) [part_number=Arduino]
  R1 = Resistor [tolerance=±0.05% resistance=330 package=THT]
  S1 = Square Pushbutton
  U1 = RELAY [package=relay-t9a]

nets:
  N1: Part2.D13/SCK, U1.COIL1
  N2: Part2.GND, R1.Pin_1, U1.COIL2
  N3: Part2.D2, R1.Pin_0, S1.leg0
  N4: Part2.5V, S1.leg1
