# Fritzing sketch esquemaRele (saved by Fritzing 0.9.1b)
breadboards: 1

parts:
  D1 = Rectifier Diode [part_number=1N4001 package="300 mil [THT]"]
  L1 = Solenoid [part_number="Bobina del relé"]
  R1 = Resistor [tolerance=±5% resistance=1k package=THT]
  Q1 = NPN-Transistor [package="TO92 [THT]"]

nets:
  N1: D1.cathode, L1.pin2, Q1.C
  5V: D1.anode, L1.pin1
  Salida Arduino: R1.Pin_0
  N2: R1.Pin_1, Q1.B
  GND: Q1.E
