# Fritzing sketch keyes-relay_arduino (saved by Fritzing 0.9.1b)
breadboards: 1

parts:
  Part1 = Arduino Uno (Rev3)  # not connected
  KY-1 = Keyes Relay [package=THT]

nets:
  N1: KY-1.signal, KY-1.power, KY-1.ground

custom parts:
  Keyes Relay: The Keyes 5V relay module is suitable for SCM development, home appliance control. It uses a 5V~12V TIL control signal which can control DC / AC signal.
